# Fritzing sketch Demo Sketch (saved by Fritzing 0.9.2b)
breadboards: 1

parts:
  pyboard1 = Micro Python pyboard [part_number=PYBv10b]
  LED1 = LED - 5mm [color="Red (633nm)" package="5 mm [THT]"]
  R1 = Resistor [tolerance=±5% resistance=100 package=THT]

nets:
  N1: pyboard1.P9A_GND, LED1.cathode
  N2: pyboard1.X1, R1.Pin_1
  N3: LED1.anode, R1.Pin_0
